// Logisim project Ta Quang Tung - Assignment 1 Circuit (v.2.13.8).circ as structural Verilog: 1 circuit, main circuit main
module main (
);

  wire and_1_out, and_2_out, and_3_out, and_4_out, and_5_out, and_6_out, and_7_out, and_8_out, and_9_out,
       and_10_out, and_11_out, and_12_out, and_13_out, and_14_out, and_15_out, and_16_out, and_17_out,
       and_18_out, and_19_out, and_20_out, and_21_out, and_22_out, and_23_out, and_24_out, and_25_out,
       and_26_out, and_27_out, and_28_out, and_29_out, and_30_out, and_31_out, and_32_out, and_33_out,
       and_34_out, and_35_out, and_36_out, and_37_out, and_38_out, and_39_out, and_40_out, and_41_out,
       and_42_out, and_43_out, and_44_out, and_45_out, and_46_out, and_47_out, and_48_out, and_49_out,
       and_50_out, and_51_out, and_52_out, and_53_out, and_54_out, and_55_out, and_56_out, and_57_out,
       and_58_out, and_59_out, and_60_out, and_61_out, and_62_out, and_63_out, and_64_out, and_65_out,
       and_66_out, and_67_out, and_68_out, and_69_out, and_70_out, and_71_out, and_72_out, and_73_out,
       and_74_out, and_75_out, and_76_out, and_77_out, and_78_out, and_79_out, and_80_out, and_81_out,
       and_82_out, and_83_out, and_84_out, and_85_out, and_86_out, and_87_out, and_88_out, and_89_out,
       and_90_out, and_91_out, and_92_out, and_93_out, and_94_out, and_95_out, and_96_out, and_97_out,
       and_98_out, and_99_out, and_100_out, and_101_out, and_102_out, and_103_out, and_104_out, and_105_out,
       and_106_out, buffer_1_out, buffer_2_out, buffer_3_out, buffer_4_out, buffer_5_out, buffer_6_out,
       buffer_7_out, buffer_8_out, buffer_9_out, buffer_10_out, buffer_11_out, buffer_12_out, buffer_13_out,
       buffer_14_out, buffer_15_out, buffer_16_out, buffer_17_out, buffer_18_out, buffer_19_out,
       buffer_20_out, buffer_21_out, buffer_22_out, buffer_23_out, buffer_24_out, buffer_25_out,
       buffer_26_out, buffer_27_out, buffer_28_out, buffer_29_out, buffer_30_out, buffer_31_out,
       buffer_32_out, buffer_33_out, buffer_34_out, buffer_35_out, buffer_36_out, button_1_out, button_2_out,
       button_3_out, button_4_out, button_5_out, button_6_out, button_7_out, button_8_out, clock_1_out,
       d_ff_1_q, d_ff_1_qn, d_ff_2_q, d_ff_2_qn, d_ff_3_q, d_ff_3_qn, d_ff_4_q, d_ff_4_qn, d_ff_5_q,
       d_ff_5_qn, d_ff_6_q, d_ff_6_qn, d_ff_7_q, d_ff_7_qn, d_ff_8_q, d_ff_8_qn, d_ff_9_q, d_ff_9_qn,
       d_ff_10_q, d_ff_10_qn, d_ff_11_q, d_ff_11_qn, d_ff_12_q, d_ff_12_qn, d_ff_13_q, d_ff_13_qn, d_ff_14_q,
       d_ff_14_qn, d_ff_15_q, d_ff_15_qn, d_ff_16_q, d_ff_16_qn, d_ff_17_q, d_ff_17_qn, d_ff_18_q,
       d_ff_18_qn, d_ff_19_q, d_ff_19_qn, d_ff_20_q, d_ff_20_qn, d_ff_21_q, d_ff_21_qn, d_ff_22_q,
       d_ff_22_qn, d_ff_23_q, d_ff_23_qn, d_ff_24_q, d_ff_24_qn, d_ff_25_q, d_ff_25_qn, d_ff_26_q,
       d_ff_26_qn, d_ff_27_q, d_ff_27_qn, d_ff_28_q, d_ff_28_qn, j_k_ff_1_q, j_k_ff_2_q, j_k_ff_3_q,
       j_k_ff_3_qn, j_k_ff_4_q, j_k_ff_4_qn, j_k_ff_5_q, j_k_ff_5_qn, j_k_ff_6_qn, j_k_ff_7_qn, j_k_ff_8_q,
       j_k_ff_9_qn, j_k_ff_10_qn, j_k_ff_11_qn, j_k_ff_12_qn, nor_1_out, nor_2_out, nor_3_out, nor_4_out,
       nor_5_out, nor_6_out, nor_7_out, nor_8_out, nor_9_out, nor_10_out, not_1_out, not_2_out, not_3_out,
       not_4_out, not_5_out, not_6_out, not_7_out, not_8_out, or_1_out, or_2_out, or_3_out, or_4_out,
       or_5_out, or_6_out, or_7_out, or_8_out, or_9_out, or_10_out, or_11_out, or_12_out, or_13_out,
       or_14_out, or_15_out, or_16_out, or_17_out, or_18_out, or_19_out, or_20_out, or_21_out, or_22_out,
       or_23_out, or_24_out, or_25_out, or_26_out, or_27_out, or_28_out, or_29_out, or_30_out, or_31_out,
       or_32_out, or_33_out, or_34_out, or_35_out, or_36_out, or_37_out, or_38_out, or_39_out, or_40_out,
       or_41_out, or_42_out, or_43_out, or_44_out, or_45_out, or_46_out, or_47_out, or_48_out, or_49_out,
       or_50_out, or_51_out, or_52_out, or_53_out;
  wire [3:0] j_k_ff_6_q, j_k_ff_7_q, j_k_ff_15_q, j_k_ff_16_q, j_k_ff_17_q, j_k_ff_18_q;

  Button button_1 (.out(button_1_out));
  Button button_2 (.out(button_2_out));
  LED led_1 (.in(nor_2_out));
  J_K_Flip_Flop j_k_ff_1 (
    .J(button_4_out), .K(button_4_out), .clk(button_4_out), .Q(j_k_ff_1_q), .preset(button_1_out));  // open: Qn, reset
  J_K_Flip_Flop j_k_ff_2 (
    .J(button_3_out), .K(button_3_out), .clk(button_3_out), .Q(j_k_ff_2_q), .preset(button_1_out));  // open: Qn, reset
  not not_1 (not_1_out, nor_1_out);
  not not_2 (not_2_out, nor_1_out);
  Button button_3 (.out(button_3_out));
  Button button_4 (.out(button_4_out));
  nor nor_1 (nor_1_out, button_1_out, nor_2_out);
  nor nor_2 (nor_2_out, nor_1_out, button_2_out);
  and and_1 (and_1_out, button_6_out, not_1_out, not_4_out);
  and and_2 (and_2_out, button_5_out, not_1_out, or_3_out);
  and and_3 (and_3_out, button_8_out, not_2_out);
  and and_4 (and_4_out, button_7_out, not_2_out);
  LED led_2 (.in(and_8_out));
  not not_3 (not_3_out, j_k_ff_2_q);
  LED led_3 (.in(and_7_out));
  Button button_5 (.out(button_5_out));
  and and_5 (and_5_out, j_k_ff_1_q, not_3_out);
  and and_6 (and_6_out, j_k_ff_1_q, j_k_ff_2_q);
  nor nor_3 (nor_3_out, nor_4_out, and_1_out);
  nor nor_4 (nor_4_out, and_2_out, nor_3_out);
  or or_1 (or_1_out, and_1_out, and_2_out);
  buf buffer_1 (buffer_1_out, buffer_3_out);
  buf buffer_2 (buffer_2_out, or_1_out);
  buf buffer_3 (buffer_3_out, buffer_2_out);
  nor nor_5 (nor_5_out, nor_6_out, and_3_out);
  nor nor_6 (nor_6_out, and_4_out, nor_5_out);
  or or_2 (or_2_out, and_3_out, and_4_out);
  LED led_4 (.in(or_20_out));
  LED led_5 (.in(or_21_out));
  nor nor_7 (nor_7_out, and_5_out, nor_8_out);
  nor nor_8 (nor_8_out, nor_7_out, and_6_out);
  buf buffer_4 (buffer_4_out, buffer_6_out);
  buf buffer_5 (buffer_5_out, buffer_4_out);
  buf buffer_6 (buffer_6_out, buffer_1_out);
  or or_3 (or_3_out, j_k_ff_3_q, j_k_ff_4_q, j_k_ff_5_q, j_k_ff_8_q);
  not not_4 (not_4_out, j_k_ff_8_q);
  buf buffer_7 (buffer_7_out, buffer_8_out);
  buf buffer_8 (buffer_8_out, or_2_out);
  buf buffer_9 (buffer_9_out, buffer_10_out);
  buf buffer_10 (buffer_10_out, buffer_7_out);
  LED led_6 (.in(or_28_out));
  LED led_7 (.in(or_24_out));
  LED led_8 (.in(or_27_out));
  buf buffer_11 (buffer_11_out, buffer_9_out);
  buf buffer_12 (buffer_12_out, buffer_11_out);
  buf buffer_13 (buffer_13_out, buffer_14_out);
  buf buffer_14 (buffer_14_out, buffer_16_out);
  buf buffer_15 (buffer_15_out, buffer_12_out);
  buf buffer_16 (buffer_16_out, buffer_19_out);
  buf buffer_17 (buffer_17_out, buffer_15_out);
  buf buffer_18 (buffer_18_out, buffer_17_out);
  buf buffer_19 (buffer_19_out, buffer_20_out);
  buf buffer_20 (buffer_20_out, buffer_22_out);
  buf buffer_21 (buffer_21_out, buffer_18_out);
  buf buffer_22 (buffer_22_out, buffer_24_out);
  buf buffer_23 (buffer_23_out, buffer_21_out);
  buf buffer_24 (buffer_24_out, buffer_27_out);
  buf buffer_25 (buffer_25_out, buffer_23_out);
  buf buffer_26 (buffer_26_out, buffer_25_out);
  buf buffer_27 (buffer_27_out, buffer_28_out);
  buf buffer_28 (buffer_28_out, buffer_26_out);
  LED led_9 (.in(j_k_ff_8_q));
  LED led_10 (.in(or_36_out));
  LED led_11 (.in(or_31_out));
  and and_7 (and_7_out, nor_2_out, nor_7_out);
  and and_8 (and_8_out, nor_2_out, nor_8_out);
  and and_9 (and_9_out, button_1_out, d_ff_1_q);
  J_K_Flip_Flop j_k_ff_3 (
    .J(1'b1), .K(1'b1), .clk(buffer_5_out), .Q(j_k_ff_3_q), .Qn(j_k_ff_3_qn), .preset(and_9_out),
    .reset(or_4_out));
  or or_4 (or_4_out, nor_1_out, and_10_out);
  and and_10 (and_10_out, button_1_out, d_ff_1_qn);
  buf buffer_29 (buffer_29_out, buffer_13_out);
  buf buffer_30 (buffer_30_out, buffer_29_out);
  buf buffer_31 (buffer_31_out, buffer_30_out);
  buf buffer_32 (buffer_32_out, buffer_31_out);
  buf buffer_33 (buffer_33_out, buffer_32_out);
  buf buffer_34 (buffer_34_out, buffer_33_out);
  buf buffer_35 (buffer_35_out, buffer_34_out);
  buf buffer_36 (buffer_36_out, buffer_35_out);
  or or_5 (or_5_out, and_24_out, and_25_out);
  Button button_6 (.out(button_6_out));
  Hex_Digit_Display hex_digit_display_1 (.value(j_k_ff_7_q));  // open: dp
  Button button_7 (.out(button_7_out));
  and and_11 (and_11_out, nor_3_out, j_k_ff_3_qn);
  and and_12 (and_12_out, nor_4_out, j_k_ff_3_q);
  and and_13 (and_13_out, nor_6_out, and_16_out);
  and and_14 (and_14_out, nor_5_out, and_16_out);
  Button button_8 (.out(button_8_out));
  Hex_Digit_Display hex_digit_display_2 (.value(j_k_ff_6_q));  // open: dp
  or or_6 (or_6_out, and_11_out, and_12_out);
  and and_15 (and_15_out, button_1_out, d_ff_2_q);
  J_K_Flip_Flop j_k_ff_4 (
    .J(or_6_out), .K(or_6_out), .clk(buffer_5_out), .Q(j_k_ff_4_q), .Qn(j_k_ff_4_qn), .preset(and_15_out),
    .reset(or_7_out));
  or or_7 (or_7_out, nor_1_out, and_17_out);
  and and_16 (and_16_out, buffer_36_out, nor_9_out, nor_10_out);
  Hex_Digit_Display hex_digit_display_3 (.value(j_k_ff_18_q));  // open: dp
  and and_17 (and_17_out, button_1_out, d_ff_2_qn);
  Hex_Digit_Display hex_digit_display_4 (.value(j_k_ff_17_q));  // open: dp
  Hex_Digit_Display hex_digit_display_5 (.value(j_k_ff_16_q));  // open: dp
  and and_18 (and_18_out, nor_3_out, and_11_out, j_k_ff_4_qn);
  and and_19 (and_19_out, nor_4_out, and_12_out, j_k_ff_4_q);
  Hex_Digit_Display hex_digit_display_6 (.value(j_k_ff_15_q));  // open: dp
  or or_8 (or_8_out, and_18_out, and_19_out);
  and and_20 (and_20_out, button_1_out, d_ff_3_q);
  J_K_Flip_Flop j_k_ff_5 (
    .J(or_8_out), .K(or_8_out), .clk(buffer_5_out), .Q(j_k_ff_5_q), .Qn(j_k_ff_5_qn), .preset(and_20_out),
    .reset(or_9_out));
  or or_9 (or_9_out, nor_1_out, and_21_out);
  and and_21 (and_21_out, button_1_out, d_ff_3_qn);
  nor nor_9 (nor_9_out, j_k_ff_6_q[0], j_k_ff_6_q[1], j_k_ff_6_q[2], j_k_ff_6_q[3]);
  nor nor_10 (nor_10_out, j_k_ff_7_q[0], j_k_ff_7_q[1], j_k_ff_7_q[2], j_k_ff_7_q[3]);
  and and_22 (and_22_out, button_1_out, d_ff_5_q);
  or or_10 (or_10_out, and_25_out, and_14_out, and_13_out, and_22_out);
  J_K_Flip_Flop j_k_ff_6 (
    .J(1'b1), .K(1'b1), .clk(buffer_12_out), .Q(j_k_ff_6_q[0]), .Qn(j_k_ff_6_qn), .preset(or_10_out),
    .reset(or_11_out));
  or or_11 (or_11_out, nor_1_out, and_24_out, and_23_out);
  and and_23 (and_23_out, button_1_out, d_ff_5_qn);
  not not_5 (not_5_out, j_k_ff_6_q[0]);
  and and_24 (and_24_out, not_5_out, j_k_ff_6_q[1], not_6_out, j_k_ff_6_q[3]);
  not not_6 (not_6_out, j_k_ff_6_q[2]);
  and and_25 (and_25_out, j_k_ff_6_q[0], j_k_ff_6_q[1], j_k_ff_6_q[2], j_k_ff_6_q[3]);
  and and_26 (and_26_out, button_1_out, d_ff_6_q);
  or or_12 (or_12_out, and_29_out, and_14_out, and_26_out);
  J_K_Flip_Flop j_k_ff_7 (
    .J(1'b1), .K(1'b1), .clk(or_5_out), .Q(j_k_ff_7_q[0]), .Qn(j_k_ff_7_qn), .preset(or_12_out),
    .reset(or_13_out));
  or or_13 (or_13_out, nor_1_out, and_28_out, and_13_out, and_27_out);
  and and_27 (and_27_out, button_1_out, d_ff_6_qn);
  not not_7 (not_7_out, j_k_ff_7_q[0]);
  and and_28 (and_28_out, not_7_out, j_k_ff_7_q[1], not_8_out, j_k_ff_7_q[3]);
  not not_8 (not_8_out, j_k_ff_7_q[2]);
  and and_29 (and_29_out, j_k_ff_7_q[0], j_k_ff_7_q[1], j_k_ff_7_q[2], j_k_ff_7_q[3]);
  and and_30 (and_30_out, nor_3_out, and_18_out, j_k_ff_5_qn);
  and and_31 (and_31_out, nor_4_out, and_19_out, j_k_ff_5_q);
  or or_14 (or_14_out, and_30_out, and_31_out);
  and and_32 (and_32_out, button_1_out, d_ff_4_q);
  J_K_Flip_Flop j_k_ff_8 (
    .J(or_14_out), .K(or_14_out), .clk(buffer_5_out), .Q(j_k_ff_8_q), .preset(and_32_out), .reset(or_15_out));  // open: Qn
  or or_15 (or_15_out, nor_1_out, and_37_out);
  and and_33 (and_33_out, nor_5_out, j_k_ff_6_qn);
  and and_34 (and_34_out, nor_6_out, j_k_ff_6_q[0]);
  and and_35 (and_35_out, nor_5_out, j_k_ff_7_qn);
  and and_36 (and_36_out, nor_6_out, j_k_ff_7_q[0]);
  and and_37 (and_37_out, button_1_out, d_ff_4_qn);
  or or_16 (or_16_out, and_33_out, and_34_out);
  J_K_Flip_Flop j_k_ff_9 (
    .J(or_16_out), .K(or_16_out), .clk(buffer_12_out), .Q(j_k_ff_6_q[1]), .Qn(j_k_ff_9_qn),
    .preset(and_38_out), .reset(or_18_out));
  or or_17 (or_17_out, and_35_out, and_36_out);
  J_K_Flip_Flop j_k_ff_10 (
    .J(or_17_out), .K(or_17_out), .clk(or_5_out), .Q(j_k_ff_7_q[1]), .Qn(j_k_ff_10_qn), .preset(and_40_out),
    .reset(or_19_out));
  D_Flip_Flop d_ff_1 (.D(j_k_ff_3_q), .clk(nor_1_out), .Q(d_ff_1_q), .Qn(d_ff_1_qn));  // open: preset, reset
  and and_38 (and_38_out, button_1_out, d_ff_7_q);
  or or_18 (or_18_out, nor_1_out, and_24_out, and_25_out, and_14_out, and_13_out, and_39_out);
  and and_39 (and_39_out, button_1_out, d_ff_7_qn);
  and and_40 (and_40_out, button_1_out, d_ff_8_q);
  or or_19 (or_19_out, nor_1_out, and_28_out, and_29_out, and_14_out, and_13_out, and_41_out);
  and and_41 (and_41_out, button_1_out, d_ff_8_qn);
  or or_20 (or_20_out, j_k_ff_3_q, or_21_out);
  and and_42 (and_42_out, nor_5_out, and_33_out, j_k_ff_9_qn);
  and and_43 (and_43_out, nor_6_out, and_34_out, j_k_ff_6_q[1]);
  and and_44 (and_44_out, nor_5_out, and_35_out, j_k_ff_10_qn);
  and and_45 (and_45_out, nor_6_out, and_36_out, j_k_ff_7_q[1]);
  D_Flip_Flop d_ff_2 (.D(j_k_ff_4_q), .clk(nor_1_out), .Q(d_ff_2_q), .Qn(d_ff_2_qn));  // open: preset, reset
  or or_21 (or_21_out, j_k_ff_4_q, or_24_out);
  or or_22 (or_22_out, and_42_out, and_43_out);
  or or_23 (or_23_out, and_44_out, and_45_out);
  and and_46 (and_46_out, j_k_ff_3_q, j_k_ff_4_q);
  or or_24 (or_24_out, and_46_out, or_27_out);
  and and_47 (and_47_out, button_1_out, d_ff_9_q);
  J_K_Flip_Flop j_k_ff_11 (
    .J(or_22_out), .K(or_22_out), .clk(buffer_12_out), .Q(j_k_ff_6_q[2]), .Qn(j_k_ff_11_qn),
    .preset(and_47_out), .reset(or_25_out));
  or or_25 (or_25_out, nor_1_out, and_24_out, and_25_out, and_14_out, and_13_out, and_48_out);
  and and_48 (and_48_out, button_1_out, d_ff_9_qn);
  and and_49 (and_49_out, button_1_out, d_ff_10_q);
  J_K_Flip_Flop j_k_ff_12 (
    .J(or_23_out), .K(or_23_out), .clk(or_5_out), .Q(j_k_ff_7_q[2]), .Qn(j_k_ff_12_qn), .preset(and_49_out),
    .reset(or_26_out));
  or or_26 (or_26_out, nor_1_out, and_28_out, and_29_out, and_14_out, and_13_out, and_50_out);
  and and_50 (and_50_out, button_1_out, d_ff_10_qn);
  D_Flip_Flop d_ff_3 (.D(j_k_ff_5_q), .clk(nor_1_out), .Q(d_ff_3_q), .Qn(d_ff_3_qn));  // open: preset, reset
  or or_27 (or_27_out, j_k_ff_5_q, or_28_out);
  and and_51 (and_51_out, nor_5_out, and_42_out, j_k_ff_11_qn);
  and and_52 (and_52_out, nor_6_out, and_43_out, j_k_ff_6_q[2]);
  and and_53 (and_53_out, nor_5_out, and_44_out, j_k_ff_12_qn);
  and and_54 (and_54_out, nor_6_out, and_45_out, j_k_ff_7_q[2]);
  D_Flip_Flop d_ff_4 (.D(j_k_ff_8_q), .clk(nor_1_out), .Q(d_ff_4_q), .Qn(d_ff_4_qn));  // open: preset, reset
  and and_55 (and_55_out, j_k_ff_3_q, j_k_ff_5_q);
  or or_28 (or_28_out, and_55_out, or_31_out);
  or or_29 (or_29_out, and_51_out, and_52_out);
  J_K_Flip_Flop j_k_ff_13 (
    .J(or_29_out), .K(or_29_out), .clk(buffer_12_out), .Q(j_k_ff_6_q[3]), .preset(or_32_out),
    .reset(or_33_out));  // open: Qn
  or or_30 (or_30_out, and_53_out, and_54_out);
  J_K_Flip_Flop j_k_ff_14 (
    .J(or_30_out), .K(or_30_out), .clk(or_5_out), .Q(j_k_ff_7_q[3]), .preset(or_34_out), .reset(or_35_out));  // open: Qn
  and and_56 (and_56_out, j_k_ff_4_q, j_k_ff_5_q);
  or or_31 (or_31_out, and_56_out, or_36_out);
  and and_57 (and_57_out, button_1_out, d_ff_11_q);
  or or_32 (or_32_out, and_25_out, and_14_out, and_57_out);
  or or_33 (or_33_out, nor_1_out, and_24_out, and_13_out, and_58_out);
  and and_58 (and_58_out, button_1_out, d_ff_11_qn);
  and and_59 (and_59_out, button_1_out, d_ff_12_q);
  or or_34 (or_34_out, and_29_out, and_14_out, and_59_out);
  or or_35 (or_35_out, nor_1_out, and_28_out, and_13_out, and_60_out);
  and and_60 (and_60_out, button_1_out, d_ff_12_qn);
  and and_61 (and_61_out, j_k_ff_3_q, j_k_ff_4_q, j_k_ff_5_q);
  or or_36 (or_36_out, and_61_out, j_k_ff_8_q);
  D_Flip_Flop d_ff_5 (.D(j_k_ff_6_q[0]), .clk(nor_1_out), .Q(d_ff_5_q), .Qn(d_ff_5_qn));  // open: preset, reset
  D_Flip_Flop d_ff_6 (.D(j_k_ff_7_q[0]), .clk(nor_1_out), .Q(d_ff_6_q), .Qn(d_ff_6_qn));  // open: preset, reset
  D_Flip_Flop d_ff_7 (.D(j_k_ff_6_q[1]), .clk(nor_1_out), .Q(d_ff_7_q), .Qn(d_ff_7_qn));  // open: preset, reset
  D_Flip_Flop d_ff_8 (.D(j_k_ff_7_q[1]), .clk(nor_1_out), .Q(d_ff_8_q), .Qn(d_ff_8_qn));  // open: preset, reset
  D_Flip_Flop d_ff_9 (.D(j_k_ff_6_q[2]), .clk(nor_1_out), .Q(d_ff_9_q), .Qn(d_ff_9_qn));  // open: preset, reset
  D_Flip_Flop d_ff_10 (.D(j_k_ff_7_q[2]), .clk(nor_1_out), .Q(d_ff_10_q), .Qn(d_ff_10_qn));  // open: preset, reset
  D_Flip_Flop d_ff_11 (.D(j_k_ff_6_q[3]), .clk(nor_1_out), .Q(d_ff_11_q), .Qn(d_ff_11_qn));  // open: preset, reset
  D_Flip_Flop d_ff_12 (.D(j_k_ff_7_q[3]), .clk(nor_1_out), .Q(d_ff_12_q), .Qn(d_ff_12_qn));  // open: preset, reset
  or or_37 (or_37_out, buffer_12_out, button_2_out);
  Clock clock_1 (.out(clock_1_out));
  and and_62 (and_62_out, j_k_ff_15_q[1], j_k_ff_15_q[3]);
  and and_63 (and_63_out, j_k_ff_16_q[1], j_k_ff_16_q[2]);
  and and_64 (and_64_out, j_k_ff_17_q[1], j_k_ff_17_q[3]);
  and and_65 (and_65_out, j_k_ff_18_q[1], j_k_ff_18_q[3]);
  and and_66 (and_66_out, button_1_out, d_ff_13_q);
  J_K_Flip_Flop j_k_ff_15 (
    .J(1'b1), .K(1'b1), .clk(and_67_out), .Q(j_k_ff_15_q[0]), .preset(and_66_out), .reset(or_38_out));  // open: Qn
  and and_67 (and_67_out, and_8_out, clock_1_out);
  or or_38 (or_38_out, and_68_out, or_37_out, and_62_out);
  and and_68 (and_68_out, button_1_out, d_ff_13_qn);
  and and_69 (and_69_out, button_1_out, d_ff_14_q);
  J_K_Flip_Flop j_k_ff_16 (
    .J(1'b1), .K(1'b1), .clk(and_62_out), .Q(j_k_ff_16_q[0]), .preset(and_69_out), .reset(or_39_out));  // open: Qn
  or or_39 (or_39_out, and_70_out, or_37_out, and_63_out);
  and and_70 (and_70_out, button_1_out, d_ff_14_qn);
  and and_71 (and_71_out, button_1_out, d_ff_15_q);
  J_K_Flip_Flop j_k_ff_17 (
    .J(1'b1), .K(1'b1), .clk(and_63_out), .Q(j_k_ff_17_q[0]), .preset(and_71_out), .reset(or_40_out));  // open: Qn
  or or_40 (or_40_out, and_72_out, or_37_out, and_64_out);
  and and_72 (and_72_out, button_1_out, d_ff_15_qn);
  and and_73 (and_73_out, button_1_out, d_ff_16_q);
  J_K_Flip_Flop j_k_ff_18 (
    .J(1'b1), .K(1'b1), .clk(and_64_out), .Q(j_k_ff_18_q[0]), .preset(and_73_out), .reset(or_41_out));  // open: Qn
  or or_41 (or_41_out, and_74_out, or_37_out, and_65_out);
  and and_74 (and_74_out, button_1_out, d_ff_16_qn);
  and and_75 (and_75_out, button_1_out, d_ff_17_q);
  J_K_Flip_Flop j_k_ff_19 (
    .J(j_k_ff_15_q[0]), .K(j_k_ff_15_q[0]), .clk(and_67_out), .Q(j_k_ff_15_q[1]), .preset(and_75_out),
    .reset(or_42_out));  // open: Qn
  or or_42 (or_42_out, and_76_out, or_37_out, and_62_out);
  and and_76 (and_76_out, button_1_out, d_ff_17_qn);
  and and_77 (and_77_out, button_1_out, d_ff_18_q);
  J_K_Flip_Flop j_k_ff_20 (
    .J(j_k_ff_16_q[0]), .K(j_k_ff_16_q[0]), .clk(and_62_out), .Q(j_k_ff_16_q[1]), .preset(and_77_out),
    .reset(or_43_out));  // open: Qn
  or or_43 (or_43_out, and_78_out, or_37_out, and_63_out);
  and and_78 (and_78_out, button_1_out, d_ff_18_qn);
  and and_79 (and_79_out, button_1_out, d_ff_19_q);
  J_K_Flip_Flop j_k_ff_21 (
    .J(j_k_ff_17_q[0]), .K(j_k_ff_17_q[0]), .clk(and_63_out), .Q(j_k_ff_17_q[1]), .preset(and_79_out),
    .reset(or_44_out));  // open: Qn
  or or_44 (or_44_out, and_80_out, or_37_out, and_64_out);
  and and_80 (and_80_out, button_1_out, d_ff_19_qn);
  and and_81 (and_81_out, button_1_out, d_ff_20_q);
  J_K_Flip_Flop j_k_ff_22 (
    .J(j_k_ff_18_q[0]), .K(j_k_ff_18_q[0]), .clk(and_64_out), .Q(j_k_ff_18_q[1]), .preset(and_81_out),
    .reset(or_45_out));  // open: Qn
  or or_45 (or_45_out, and_82_out, or_37_out, and_65_out);
  and and_82 (and_82_out, button_1_out, d_ff_20_qn);
  and and_83 (and_83_out, j_k_ff_15_q[0], j_k_ff_15_q[1]);
  and and_84 (and_84_out, j_k_ff_16_q[0], j_k_ff_16_q[1]);
  and and_85 (and_85_out, j_k_ff_17_q[0], j_k_ff_17_q[1]);
  and and_86 (and_86_out, j_k_ff_18_q[0], j_k_ff_18_q[1]);
  and and_87 (and_87_out, button_1_out, d_ff_21_q);
  J_K_Flip_Flop j_k_ff_23 (
    .J(and_83_out), .K(and_83_out), .clk(and_67_out), .Q(j_k_ff_15_q[2]), .preset(and_87_out),
    .reset(or_46_out));  // open: Qn
  or or_46 (or_46_out, and_88_out, or_37_out, and_62_out);
  and and_88 (and_88_out, button_1_out, d_ff_21_qn);
  and and_89 (and_89_out, button_1_out, d_ff_22_q);
  J_K_Flip_Flop j_k_ff_24 (
    .J(and_84_out), .K(and_84_out), .clk(and_62_out), .Q(j_k_ff_16_q[2]), .preset(and_89_out),
    .reset(or_47_out));  // open: Qn
  or or_47 (or_47_out, and_90_out, or_37_out, and_63_out);
  and and_90 (and_90_out, button_1_out, d_ff_22_qn);
  and and_91 (and_91_out, button_1_out, d_ff_23_q);
  J_K_Flip_Flop j_k_ff_25 (
    .J(and_85_out), .K(and_85_out), .clk(and_63_out), .Q(j_k_ff_17_q[2]), .preset(and_91_out),
    .reset(or_48_out));  // open: Qn
  or or_48 (or_48_out, and_92_out, or_37_out, and_64_out);
  and and_92 (and_92_out, button_1_out, d_ff_23_qn);
  and and_93 (and_93_out, button_1_out, d_ff_24_q);
  J_K_Flip_Flop j_k_ff_26 (
    .J(and_86_out), .K(and_86_out), .clk(and_64_out), .Q(j_k_ff_18_q[2]), .preset(and_93_out),
    .reset(or_49_out));  // open: Qn
  or or_49 (or_49_out, and_94_out, or_37_out, and_65_out);
  and and_94 (and_94_out, button_1_out, d_ff_24_qn);
  and and_95 (and_95_out, and_83_out, j_k_ff_15_q[2]);
  and and_96 (and_96_out, and_84_out, j_k_ff_16_q[2]);
  and and_97 (and_97_out, and_85_out, j_k_ff_17_q[2]);
  and and_98 (and_98_out, and_86_out, j_k_ff_18_q[2]);
  and and_99 (and_99_out, button_1_out, d_ff_25_q);
  J_K_Flip_Flop j_k_ff_27 (
    .J(and_95_out), .K(and_95_out), .clk(and_67_out), .Q(j_k_ff_15_q[3]), .preset(and_99_out),
    .reset(or_50_out));  // open: Qn
  or or_50 (or_50_out, and_100_out, or_37_out, and_62_out);
  and and_100 (and_100_out, button_1_out, d_ff_25_qn);
  and and_101 (and_101_out, button_1_out, d_ff_26_q);
  J_K_Flip_Flop j_k_ff_28 (
    .J(and_96_out), .K(and_96_out), .clk(and_62_out), .Q(j_k_ff_16_q[3]), .preset(and_101_out),
    .reset(or_51_out));  // open: Qn
  or or_51 (or_51_out, and_102_out, or_37_out, and_63_out);
  and and_102 (and_102_out, button_1_out, d_ff_26_qn);
  and and_103 (and_103_out, button_1_out, d_ff_27_q);
  J_K_Flip_Flop j_k_ff_29 (
    .J(and_97_out), .K(and_97_out), .clk(and_63_out), .Q(j_k_ff_17_q[3]), .preset(and_103_out),
    .reset(or_52_out));  // open: Qn
  or or_52 (or_52_out, and_104_out, or_37_out, and_64_out);
  and and_104 (and_104_out, button_1_out, d_ff_27_qn);
  and and_105 (and_105_out, button_1_out, d_ff_28_q);
  J_K_Flip_Flop j_k_ff_30 (
    .J(and_98_out), .K(and_98_out), .clk(and_64_out), .Q(j_k_ff_18_q[3]), .preset(and_105_out),
    .reset(or_53_out));  // open: Qn
  or or_53 (or_53_out, and_106_out, or_37_out, and_65_out);
  and and_106 (and_106_out, button_1_out, d_ff_28_qn);
  D_Flip_Flop d_ff_13 (.D(j_k_ff_15_q[0]), .clk(button_2_out), .Q(d_ff_13_q), .Qn(d_ff_13_qn));  // open: preset, reset
  D_Flip_Flop d_ff_14 (.D(j_k_ff_16_q[0]), .clk(button_2_out), .Q(d_ff_14_q), .Qn(d_ff_14_qn));  // open: preset, reset
  D_Flip_Flop d_ff_15 (.D(j_k_ff_17_q[0]), .clk(button_2_out), .Q(d_ff_15_q), .Qn(d_ff_15_qn));  // open: preset, reset
  D_Flip_Flop d_ff_16 (.D(j_k_ff_18_q[0]), .clk(button_2_out), .Q(d_ff_16_q), .Qn(d_ff_16_qn));  // open: preset, reset
  D_Flip_Flop d_ff_17 (.D(j_k_ff_15_q[1]), .clk(button_2_out), .Q(d_ff_17_q), .Qn(d_ff_17_qn));  // open: preset, reset
  D_Flip_Flop d_ff_18 (.D(j_k_ff_16_q[1]), .clk(button_2_out), .Q(d_ff_18_q), .Qn(d_ff_18_qn));  // open: preset, reset
  D_Flip_Flop d_ff_19 (.D(j_k_ff_17_q[1]), .clk(button_2_out), .Q(d_ff_19_q), .Qn(d_ff_19_qn));  // open: preset, reset
  D_Flip_Flop d_ff_20 (.D(j_k_ff_18_q[1]), .clk(button_2_out), .Q(d_ff_20_q), .Qn(d_ff_20_qn));  // open: preset, reset
  D_Flip_Flop d_ff_21 (.D(j_k_ff_15_q[2]), .clk(button_2_out), .Q(d_ff_21_q), .Qn(d_ff_21_qn));  // open: preset, reset
  D_Flip_Flop d_ff_22 (.D(j_k_ff_16_q[2]), .clk(button_2_out), .Q(d_ff_22_q), .Qn(d_ff_22_qn));  // open: preset, reset
  D_Flip_Flop d_ff_23 (.D(j_k_ff_17_q[2]), .clk(button_2_out), .Q(d_ff_23_q), .Qn(d_ff_23_qn));  // open: preset, reset
  D_Flip_Flop d_ff_24 (.D(j_k_ff_18_q[2]), .clk(button_2_out), .Q(d_ff_24_q), .Qn(d_ff_24_qn));  // open: preset, reset
  D_Flip_Flop d_ff_25 (.D(j_k_ff_15_q[3]), .clk(button_2_out), .Q(d_ff_25_q), .Qn(d_ff_25_qn));  // open: preset, reset
  D_Flip_Flop d_ff_26 (.D(j_k_ff_16_q[3]), .clk(button_2_out), .Q(d_ff_26_q), .Qn(d_ff_26_qn));  // open: preset, reset
  D_Flip_Flop d_ff_27 (.D(j_k_ff_17_q[3]), .clk(button_2_out), .Q(d_ff_27_q), .Qn(d_ff_27_qn));  // open: preset, reset
  D_Flip_Flop d_ff_28 (.D(j_k_ff_18_q[3]), .clk(button_2_out), .Q(d_ff_28_q), .Qn(d_ff_28_qn));  // open: preset, reset

  // Notes on the sheet:
  //   OFF
  //   ON
  //   ON PULSE
  //   OFF PULSE
  //   ON PULSE
  //   PLAY PULSE
  //   PAUSE PULSE
  //   off signal
  //   on pulse
  //   vol up pulse
  //   vol down pulse
  //   off signal
  //   on pulse
  //   ON
  //   track up pulse
  //   track down pulse
  //   PAUSE
  //   PLAY
  //   PLAYING
  //   IS OFF
  //   IS ON
  //   ON SIGNAL
  //   --
  //   PAUSED
  //   VOLUME
  //   PAUSED
  //   PLAYING
  //   ++
  //   PREV
  //   TRACK
  //   NEXT
  //   NOTE: To simulate playing, enable auto clock ticks and set the tick frequency to 2.0Hz
  //   TIME
  //   :
  //   8
  //   4
  //   2
  //   1
  //   off pulse
  //   on pulse
  //   is playing signal
  //   track change pulse
endmodule
