// Logisim project new.circ as structural Verilog: 1 circuit, main circuit main
module main (
  input  PAUSE,
  input  PLAY,
  input  PAUSE_2,
  input  PLAY_2,
  input  in_5,
  input  in_6,
  input  in_7,
  input  in_8,
  input  in_9,
  input  in_10,
  input  in_11,
  input  in_12,
  input  in_13,
  input  in_14,
  input  in_15,
  input  in_16,
  input  in_17,
  input  in_18,
  input  in_19,
  input  in_20,
  input  in_21,
  input  in_22,
  input  in_23,
  input  in_24,
  input  in_25,
  input  in_26,
  input  in_27,
  input  in_28,
  input  in_29,
  input  in_30,
  input  in_31,
  input  in_32,
  input  in_33,
  input  in_34,
  input  in_35,
  input  in_36,
  input  in_37,
  input  in_38,
  input  in_39,
  input  in_40,
  input  in_41,
  input  in_42,
  input  in_43,
  input  in_44,
  input  in_45,
  input  in_46,
  input  in_47,
  input  in_48,
  input  in_49,
  input  in_50,
  input  in_51,
  input  in_52,
  input  in_53,
  output out_54
);

  wire and_1_out, and_2_out, and_3_out, and_4_out, and_5_out, and_6_out, and_7_out, and_8_out, and_9_out,
       and_10_out, and_11_out, and_12_out, and_13_out, and_14_out, and_15_out, and_16_out, and_17_out,
       and_18_out, and_19_out, and_20_out, and_21_out, and_22_out, and_23_out, and_24_out, and_25_out,
       and_26_out, and_27_out, and_28_out, and_29_out, and_30_out, and_31_out, and_32_out, and_33_out,
       and_34_out, and_35_out, and_36_out, and_37_out, and_38_out, and_39_out, and_40_out, and_41_out,
       and_42_out, and_43_out, and_44_out, and_45_out, and_46_out, and_47_out, and_49_out, and_50_out,
       and_51_out, and_52_out, and_53_out, and_54_out, and_55_out, and_56_out, and_57_out, and_58_out,
       and_59_out, and_60_out, and_61_out, and_62_out, and_63_out, and_64_out, and_65_out, and_66_out,
       and_67_out, and_68_out, and_69_out, and_70_out, and_71_out, and_72_out, and_73_out, and_74_out,
       and_75_out, and_76_out, and_77_out, and_78_out, and_79_out, and_80_out, and_81_out, and_82_out,
       and_83_out, and_84_out, and_85_out, and_86_out, and_87_out, and_88_out, and_89_out, and_90_out,
       and_91_out, and_92_out, and_93_out, and_94_out, and_95_out, and_96_out, and_97_out, and_98_out,
       and_99_out, and_100_out, and_101_out, and_102_out, and_103_out, and_104_out, and_105_out, and_106_out,
       and_107_out, and_108_out, and_109_out, and_110_out, and_111_out, and_112_out, and_113_out,
       and_114_out, and_115_out, and_116_out, and_117_out, and_118_out, and_119_out, and_120_out,
       and_121_out, and_122_out, and_123_out, and_124_out, and_125_out, and_126_out, and_127_out,
       and_128_out, and_129_out, and_130_out, and_131_out, and_132_out, and_133_out, and_134_out,
       and_135_out, and_136_out, and_137_out, and_138_out, and_139_out, and_140_out, and_141_out,
       and_142_out, and_143_out, and_144_out, and_145_out, and_146_out, and_147_out, and_148_out,
       and_149_out, and_150_out, and_151_out, and_152_out, and_153_out, and_154_out, and_155_out,
       and_156_out, and_157_out, and_158_out, and_159_out, and_160_out, and_161_out, and_162_out,
       and_163_out, and_164_out, and_165_out, and_166_out, and_167_out, and_168_out, and_169_out,
       and_170_out, and_171_out, and_172_out, and_173_out, and_174_out, and_175_out, and_176_out,
       and_177_out, and_178_out, and_179_out, and_180_out, and_181_out, and_182_out, and_183_out,
       and_184_out, and_185_out, and_186_out, and_187_out, and_188_out, and_189_out, and_190_out,
       and_191_out, and_192_out, and_193_out, and_194_out, and_195_out, and_196_out, and_197_out,
       and_198_out, buffer_1_out, buffer_2_out, buffer_3_out, buffer_4_out, buffer_5_out, buffer_6_out,
       buffer_7_out, buffer_8_out, buffer_9_out, buffer_10_out, buffer_11_out, buffer_12_out, buffer_13_out,
       buffer_14_out, buffer_15_out, buffer_16_out, buffer_17_out, buffer_18_out, buffer_19_out,
       buffer_20_out, buffer_21_out, buffer_22_out, buffer_23_out, buffer_24_out, buffer_25_out,
       buffer_26_out, buffer_27_out, buffer_28_out, buffer_29_out, buffer_30_out, buffer_31_out,
       buffer_32_out, buffer_33_out, buffer_34_out, buffer_35_out, buffer_36_out, buffer_37_out,
       buffer_38_out, buffer_39_out, buffer_40_out, buffer_41_out, button_1_out, button_2_out, button_3_out,
       button_4_out, button_6_out, button_7_out, button_8_out, button_9_out, button_10_out, button_11_out,
       button_12_out, button_13_out, button_14_out, button_15_out, button_16_out, button_17_out, d_ff_1_q,
       d_ff_2_q, d_ff_3_q, d_ff_4_q, d_ff_5_q, d_ff_6_q, d_ff_7_q, j_k_ff_1_q, j_k_ff_3_q, j_k_ff_5_q,
       j_k_ff_7_q, j_k_ff_9_q, j_k_ff_11_q, j_k_ff_15_q, j_k_ff_17_q, j_k_ff_20_q, j_k_ff_22_q, j_k_ff_24_q,
       j_k_ff_25_q, j_k_ff_26_q, j_k_ff_28_q, j_k_ff_30_q, j_k_ff_31_q, j_k_ff_33_q, j_k_ff_35_q,
       j_k_ff_37_q, j_k_ff_39_q, j_k_ff_41_q, j_k_ff_43_q, j_k_ff_45_q, j_k_ff_47_q, j_k_ff_52_q,
       j_k_ff_55_q, j_k_ff_58_q, j_k_ff_59_q, j_k_ff_63_q, j_k_ff_69_q, j_k_ff_73_q, nor_1_out, nor_2_out,
       nor_3_out, nor_4_out, nor_5_out, nor_6_out, nor_7_out, nor_8_out, nor_9_out, nor_10_out, nor_11_out,
       nor_12_out, nor_13_out, nor_14_out, nor_15_out, nor_16_out, nor_17_out, nor_18_out, nor_19_out,
       nor_20_out, nor_21_out, nor_22_out, nor_23_out, nor_24_out, nor_25_out, nor_26_out, not_1_out,
       not_2_out, not_3_out, not_4_out, not_5_out, not_6_out, not_7_out, not_8_out, not_9_out, not_10_out,
       not_11_out, not_12_out, not_13_out, not_14_out, not_15_out, not_16_out, not_17_out, not_18_out,
       not_19_out, not_20_out, not_21_out, not_22_out, not_23_out, not_24_out, not_25_out, not_26_out,
       not_27_out, not_28_out, not_29_out, not_30_out, not_31_out, not_32_out, not_33_out, not_34_out,
       not_35_out, not_36_out, not_37_out, not_38_out, not_39_out, not_40_out, not_41_out, not_42_out,
       not_43_out, not_44_out, not_45_out, not_46_out, not_47_out, not_48_out, not_49_out, not_50_out,
       not_51_out, not_52_out, not_53_out, not_54_out, not_55_out, not_56_out, not_57_out, not_58_out,
       not_59_out, not_60_out, not_61_out, not_62_out, not_63_out, not_64_out, not_65_out, not_66_out,
       not_67_out, not_68_out, not_69_out, not_70_out, not_71_out, not_72_out, not_73_out, not_74_out,
       not_75_out, not_76_out, not_77_out, not_78_out, not_79_out, not_80_out, not_81_out, not_82_out,
       not_83_out, not_84_out, not_85_out, not_86_out, not_87_out, not_88_out, not_89_out, not_90_out,
       not_91_out, not_92_out, not_93_out, not_94_out, not_95_out, not_96_out, not_97_out, not_98_out,
       not_99_out, not_100_out, not_101_out, not_102_out, not_103_out, not_104_out, or_1_out, or_2_out,
       or_3_out, or_4_out, or_5_out, or_6_out, or_7_out, or_8_out, or_9_out, or_10_out, or_11_out, or_12_out,
       or_13_out, or_14_out, or_15_out, or_16_out, or_17_out, or_18_out, or_19_out, or_20_out, or_21_out,
       or_22_out, or_23_out, or_24_out, or_25_out, or_26_out, or_27_out, or_28_out, or_29_out, or_30_out,
       or_31_out, or_32_out, or_33_out, or_34_out, or_35_out, or_36_out, or_37_out, or_38_out, or_39_out,
       or_40_out, or_41_out, or_42_out, or_43_out, or_44_out, or_45_out, or_46_out, or_47_out, or_48_out,
       or_49_out, or_50_out, or_51_out, or_52_out, or_53_out, or_54_out, or_55_out, or_56_out, or_57_out,
       or_58_out, or_59_out, or_60_out, or_61_out, or_62_out, or_63_out, or_64_out, or_65_out, or_66_out,
       or_67_out, or_68_out, undriven, undriven_2, undriven_3, undriven_4, undriven_5, undriven_6;
  wire [2:0] j_k_ff_13_q;
  wire [3:0] j_k_ff_2_q, j_k_ff_10_q, j_k_ff_12_q, j_k_ff_32_q, j_k_ff_34_q, j_k_ff_48_q, j_k_ff_49_q,
       j_k_ff_60_q, j_k_ff_61_q, j_k_ff_62_q;

  and and_1 (and_1_out, PAUSE, PLAY);
  not not_1 (not_1_out, PAUSE);
  and and_2 (and_2_out, not_1_out, PLAY);
  Button button_1 (.out(button_1_out));
  and and_3 (and_3_out, PAUSE_2, PLAY_2);
  and and_4 (and_4_out, in_5, PLAY_2);
  Button button_2 (.out(button_2_out));
  J_K_Flip_Flop j_k_ff_1 (
    .J(in_10), .K(in_10), .clk(button_1_out), .Q(j_k_ff_1_q), .preset(and_5_out), .reset(and_6_out));  // open: Qn
  J_K_Flip_Flop j_k_ff_2 (
    .J(in_10), .K(in_10), .clk(button_2_out), .Q(j_k_ff_2_q[0]), .preset(and_7_out), .reset(and_8_out));  // open: Qn
  nor nor_1 (nor_1_out, and_9_out, nor_2_out);
  nor nor_2 (nor_2_out, nor_1_out, and_10_out);
  Button button_3 (.out(button_3_out));
  Button button_4 (.out(button_4_out));
  nor nor_3 (nor_3_out, and_1_out, nor_4_out);
  nor nor_4 (nor_4_out, nor_3_out, and_2_out);
  nor nor_5 (nor_5_out, and_3_out, nor_6_out);
  nor nor_6 (nor_6_out, nor_5_out, and_4_out);
  and and_5 (and_5_out, button_2_out, j_k_ff_2_q[0]);
  and and_6 (and_6_out, button_2_out, not_2_out);
  not not_2 (not_2_out, j_k_ff_2_q[0]);
  and and_7 (and_7_out, button_1_out, j_k_ff_1_q);
  and and_8 (and_8_out, button_1_out, not_3_out);
  not not_3 (not_3_out, j_k_ff_1_q);
  Button button_5 (.out(out_54));
  buf buffer_1 (buffer_1_out, button_3_out);
  D_Flip_Flop d_ff_1 (.D(in_46), .clk(button_3_out), .Q(d_ff_1_q));  // open: Qn, preset, reset
  buf buffer_2 (buffer_2_out, button_4_out);
  D_Flip_Flop d_ff_2 (.D(in_49), .clk(button_4_out), .Q(d_ff_2_q));  // open: Qn, preset, reset
  LED led_1 (.in(nor_3_out));
  LED led_2 (.in(nor_4_out));
  LED led_3 (.in(nor_5_out));
  LED led_4 (.in(nor_6_out));
  not not_4 (not_4_out, j_k_ff_2_q[0]);
  and and_9 (and_9_out, undriven, undriven);
  and and_10 (and_10_out, undriven, not_7_out);
  buf buffer_3 (buffer_3_out, buffer_5_out);
  buf buffer_4 (buffer_4_out, buffer_1_out);
  buf buffer_5 (buffer_5_out, buffer_4_out);
  buf buffer_6 (buffer_6_out, buffer_3_out);
  buf buffer_7 (buffer_7_out, buffer_2_out);
  not not_5 (not_5_out, button_6_out);
  Button button_6 (.out(button_6_out));
  not not_6 (not_6_out, button_7_out);
  Button button_7 (.out(button_7_out));
  D_Flip_Flop d_ff_3 (.D(d_ff_1_q), .clk(buffer_8_out), .Q(d_ff_3_q));  // open: Qn, preset, reset
  buf buffer_8 (buffer_8_out, buffer_9_out);
  buf buffer_9 (buffer_9_out, buffer_6_out);
  D_Flip_Flop d_ff_4 (.D(d_ff_2_q), .clk(buffer_7_out), .Q(d_ff_4_q));  // open: Qn, preset, reset
  nor nor_7 (nor_7_out, button_6_out, nor_8_out);
  nor nor_8 (nor_8_out, nor_7_out, not_5_out);
  buf buffer_10 (buffer_10_out, buffer_12_out);
  buf buffer_11 (buffer_11_out, buffer_10_out);
  buf buffer_12 (buffer_12_out, buffer_13_out);
  buf buffer_13 (buffer_13_out, button_6_out);
  nor nor_9 (nor_9_out, button_7_out, nor_10_out);
  nor nor_10 (nor_10_out, nor_9_out, not_6_out);
  and and_11 (and_11_out, button_2_out, j_k_ff_2_q[1]);
  J_K_Flip_Flop j_k_ff_3 (
    .J(j_k_ff_1_q), .K(j_k_ff_1_q), .clk(button_1_out), .Q(j_k_ff_3_q), .preset(and_11_out),
    .reset(and_12_out));  // open: Qn
  and and_12 (and_12_out, button_2_out, not_8_out);
  and and_13 (and_13_out, button_1_out, j_k_ff_3_q);
  J_K_Flip_Flop j_k_ff_4 (
    .J(not_4_out), .K(not_4_out), .clk(button_2_out), .Q(j_k_ff_2_q[1]), .preset(and_13_out),
    .reset(and_14_out));  // open: Qn
  and and_14 (and_14_out, button_1_out, not_9_out);
  not not_7 (not_7_out, undriven);
  buf buffer_14 (buffer_14_out, buffer_16_out);
  buf buffer_15 (buffer_15_out, buffer_14_out);
  buf buffer_16 (buffer_16_out, buffer_11_out);
  not not_8 (not_8_out, j_k_ff_2_q[1]);
  not not_9 (not_9_out, j_k_ff_3_q);
  D_Flip_Flop d_ff_5 (.D(nor_8_out), .clk(buffer_15_out), .Q(d_ff_5_q));  // open: Qn, preset, reset
  D_Flip_Flop d_ff_6 (.D(nor_10_out), .clk(button_7_out), .Q(d_ff_6_q));  // open: Qn, preset, reset
  not not_10 (not_10_out, j_k_ff_2_q[1]);
  and and_15 (and_15_out, j_k_ff_1_q, j_k_ff_3_q);
  and and_16 (and_16_out, not_4_out, not_10_out);
  nor nor_11 (nor_11_out, and_21_out, nor_12_out);
  nor nor_12 (nor_12_out, nor_11_out, and_22_out);
  nor nor_13 (nor_13_out, and_23_out, nor_14_out);
  nor nor_14 (nor_14_out, nor_13_out, and_24_out);
  and and_17 (and_17_out, button_2_out, j_k_ff_2_q[2]);
  J_K_Flip_Flop j_k_ff_5 (
    .J(and_15_out), .K(and_15_out), .clk(button_1_out), .Q(j_k_ff_5_q), .preset(and_17_out),
    .reset(and_18_out));  // open: Qn
  and and_18 (and_18_out, button_2_out, not_11_out);
  not not_11 (not_11_out, j_k_ff_2_q[2]);
  and and_19 (and_19_out, button_1_out, j_k_ff_5_q);
  J_K_Flip_Flop j_k_ff_6 (
    .J(and_16_out), .K(and_16_out), .clk(button_2_out), .Q(j_k_ff_2_q[2]), .preset(and_19_out),
    .reset(and_20_out));  // open: Qn
  and and_20 (and_20_out, button_1_out, not_12_out);
  not not_12 (not_12_out, j_k_ff_5_q);
  not not_13 (not_13_out, j_k_ff_2_q[2]);
  and and_21 (and_21_out, undriven_3, undriven_3);
  and and_22 (and_22_out, undriven_3, not_14_out);
  and and_23 (and_23_out, undriven_2, undriven_2);
  and and_24 (and_24_out, undriven_2, not_15_out);
  and and_25 (and_25_out, and_15_out, j_k_ff_5_q);
  and and_26 (and_26_out, and_16_out, not_13_out);
  not not_14 (not_14_out, undriven_3);
  not not_15 (not_15_out, undriven_2);
  and and_27 (and_27_out, button_2_out, j_k_ff_2_q[3]);
  J_K_Flip_Flop j_k_ff_7 (
    .J(and_25_out), .K(and_25_out), .clk(button_1_out), .Q(j_k_ff_7_q), .preset(and_27_out),
    .reset(and_28_out));  // open: Qn
  and and_28 (and_28_out, button_2_out, not_16_out);
  not not_16 (not_16_out, j_k_ff_2_q[3]);
  and and_29 (and_29_out, button_1_out, j_k_ff_7_q);
  J_K_Flip_Flop j_k_ff_8 (
    .J(and_26_out), .K(and_26_out), .clk(button_2_out), .Q(j_k_ff_2_q[3]), .preset(and_29_out),
    .reset(and_30_out));  // open: Qn
  and and_30 (and_30_out, button_1_out, not_17_out);
  not not_17 (not_17_out, j_k_ff_7_q);
  Button button_8 (.out(button_8_out));
  buf buffer_17 (buffer_17_out, and_39_out);
  buf buffer_18 (buffer_18_out, buffer_17_out);
  buf buffer_19 (buffer_19_out, and_40_out);
  buf buffer_20 (buffer_20_out, buffer_19_out);
  buf buffer_21 (buffer_21_out, buffer_18_out);
  buf buffer_22 (buffer_22_out, buffer_21_out);
  buf buffer_23 (buffer_23_out, buffer_20_out);
  buf buffer_24 (buffer_24_out, buffer_23_out);
  buf buffer_25 (buffer_25_out, buffer_22_out);
  buf buffer_26 (buffer_26_out, buffer_24_out);
  buf buffer_27 (buffer_27_out, buffer_25_out);
  buf buffer_28 (buffer_28_out, buffer_26_out);
  buf buffer_29 (buffer_29_out, buffer_27_out);
  buf buffer_30 (buffer_30_out, buffer_29_out);
  buf buffer_31 (buffer_31_out, buffer_28_out);
  buf buffer_32 (buffer_32_out, buffer_30_out);
  buf buffer_33 (buffer_33_out, buffer_31_out);
  buf buffer_34 (buffer_34_out, buffer_32_out);
  buf buffer_35 (buffer_35_out, buffer_33_out);
  buf buffer_36 (buffer_36_out, buffer_35_out);
  buf buffer_37 (buffer_37_out, buffer_34_out);
  buf buffer_38 (buffer_38_out, buffer_36_out);
  buf buffer_39 (buffer_39_out, buffer_37_out);
  buf buffer_40 (buffer_40_out, buffer_39_out);
  buf buffer_41 (buffer_41_out, buffer_38_out);
  Hex_Digit_Display hex_digit_display_1 (.value(j_k_ff_2_q));  // open: dp
  Button button_9 (.out(button_9_out));
  and and_31 (and_31_out, and_40_out, in_21);
  J_K_Flip_Flop j_k_ff_9 (
    .J(in_24), .K(in_24), .clk(button_8_out), .Q(j_k_ff_9_q), .preset(or_1_out), .reset(or_2_out));  // open: Qn
  and and_32 (and_32_out, and_40_out, in_33);
  J_K_Flip_Flop j_k_ff_10 (
    .J(in_24), .K(in_24), .clk(button_9_out), .Q(j_k_ff_10_q[0]), .preset(or_3_out), .reset(or_4_out));  // open: Qn
  and and_33 (and_33_out, and_46_out, in_41);
  J_K_Flip_Flop j_k_ff_11 (
    .J(in_45), .K(in_45), .clk(and_39_out), .Q(j_k_ff_11_q), .preset(or_5_out), .reset(or_6_out));  // open: Qn
  and and_34 (and_34_out, and_46_out, in_52);
  J_K_Flip_Flop j_k_ff_12 (
    .J(in_45), .K(in_45), .clk(and_40_out), .Q(j_k_ff_12_q[0]), .preset(or_7_out), .reset(or_8_out));  // open: Qn
  and and_35 (and_35_out, button_9_out, j_k_ff_10_q[0]);
  or or_1 (or_1_out, and_31_out, and_35_out);
  or or_2 (or_2_out, and_39_out, and_36_out);
  and and_36 (and_36_out, button_9_out, not_18_out);
  not not_18 (not_18_out, j_k_ff_10_q[0]);
  and and_37 (and_37_out, button_8_out, j_k_ff_9_q);
  or or_3 (or_3_out, and_32_out, and_37_out);
  or or_4 (or_4_out, and_39_out, and_38_out);
  and and_38 (and_38_out, button_8_out, not_19_out);
  not not_19 (not_19_out, j_k_ff_9_q);
  and and_39 (and_39_out, not_23_out, j_k_ff_10_q[1], not_37_out, j_k_ff_10_q[3]);
  and and_40 (and_40_out, j_k_ff_10_q[0], j_k_ff_10_q[1], j_k_ff_10_q[2], j_k_ff_10_q[3]);
  and and_41 (and_41_out, buffer_41_out, j_k_ff_12_q[0]);
  or or_5 (or_5_out, and_33_out, and_41_out);
  or or_6 (or_6_out, and_45_out, and_42_out);
  and and_42 (and_42_out, buffer_41_out, not_20_out);
  not not_20 (not_20_out, j_k_ff_12_q[0]);
  and and_43 (and_43_out, buffer_40_out, j_k_ff_11_q);
  or or_7 (or_7_out, and_34_out, and_43_out);
  or or_8 (or_8_out, and_45_out, and_44_out);
  and and_44 (and_44_out, buffer_40_out, not_21_out);
  not not_21 (not_21_out, j_k_ff_11_q);
  and and_45 (and_45_out, not_25_out, j_k_ff_12_q[1], not_40_out, j_k_ff_12_q[3]);
  and and_46 (and_46_out, j_k_ff_12_q[0], j_k_ff_12_q[1], j_k_ff_12_q[2], j_k_ff_12_q[3]);
  J_K_Flip_Flop j_k_ff_13 (
    .J(in_8), .K(in_8), .clk(button_10_out), .Q(j_k_ff_13_q[0]), .preset(and_49_out));  // open: Qn, reset
  Button button_10 (.out(button_10_out));
  and and_47 (and_47_out, j_k_ff_13_q[0], j_k_ff_13_q[1], j_k_ff_13_q[2]);
  // AND_Gate and_48 has open pins: in0=j_k_ff_13_q[0], in1=j_k_ff_13_q[1], in2=not_26_out, out=open
  not not_22 (not_22_out, j_k_ff_10_q[0]);
  not not_23 (not_23_out, j_k_ff_10_q[0]);
  not not_24 (not_24_out, j_k_ff_12_q[0]);
  not not_25 (not_25_out, j_k_ff_12_q[0]);
  and and_49 (and_49_out, and_47_out, in_6);
  not not_26 (not_26_out, j_k_ff_13_q[2]);
  J_K_Flip_Flop j_k_ff_14 (
    .J(not_27_out), .K(not_27_out), .clk(button_10_out), .Q(j_k_ff_13_q[1]), .reset(and_47_out));  // open: Qn, preset
  not not_27 (not_27_out, j_k_ff_13_q[0]);
  and and_50 (and_50_out, button_9_out, j_k_ff_10_q[1]);
  J_K_Flip_Flop j_k_ff_15 (
    .J(j_k_ff_9_q), .K(j_k_ff_9_q), .clk(button_8_out), .Q(j_k_ff_15_q), .preset(and_50_out), .reset(or_9_out));  // open: Qn
  or or_9 (or_9_out, and_39_out, and_40_out, and_51_out);
  and and_51 (and_51_out, button_9_out, not_28_out);
  and and_52 (and_52_out, button_8_out, j_k_ff_15_q);
  J_K_Flip_Flop j_k_ff_16 (
    .J(not_22_out), .K(not_22_out), .clk(button_9_out), .Q(j_k_ff_10_q[1]), .preset(and_52_out),
    .reset(or_10_out));  // open: Qn
  or or_10 (or_10_out, and_39_out, and_40_out, and_53_out);
  and and_53 (and_53_out, button_8_out, not_29_out);
  and and_54 (and_54_out, buffer_41_out, j_k_ff_12_q[1]);
  J_K_Flip_Flop j_k_ff_17 (
    .J(j_k_ff_11_q), .K(j_k_ff_11_q), .clk(and_39_out), .Q(j_k_ff_17_q), .preset(and_54_out),
    .reset(or_11_out));  // open: Qn
  or or_11 (or_11_out, and_45_out, and_46_out, and_55_out);
  and and_55 (and_55_out, buffer_41_out, not_30_out);
  and and_56 (and_56_out, buffer_40_out, j_k_ff_17_q);
  J_K_Flip_Flop j_k_ff_18 (
    .J(not_24_out), .K(not_24_out), .clk(and_40_out), .Q(j_k_ff_12_q[1]), .preset(and_56_out),
    .reset(or_12_out));  // open: Qn
  or or_12 (or_12_out, and_45_out, and_46_out, and_57_out);
  and and_57 (and_57_out, buffer_40_out, not_31_out);
  not not_28 (not_28_out, j_k_ff_10_q[1]);
  not not_29 (not_29_out, j_k_ff_15_q);
  not not_30 (not_30_out, j_k_ff_12_q[1]);
  not not_31 (not_31_out, j_k_ff_17_q);
  not not_32 (not_32_out, j_k_ff_13_q[1]);
  not not_33 (not_33_out, j_k_ff_10_q[1]);
  not not_34 (not_34_out, j_k_ff_12_q[1]);
  and and_58 (and_58_out, not_27_out, not_32_out);
  and and_59 (and_59_out, j_k_ff_9_q, j_k_ff_15_q);
  and and_60 (and_60_out, not_22_out, not_33_out);
  and and_61 (and_61_out, j_k_ff_11_q, j_k_ff_17_q);
  and and_62 (and_62_out, not_24_out, not_34_out);
  and and_63 (and_63_out, and_47_out, in_7);
  J_K_Flip_Flop j_k_ff_19 (
    .J(and_58_out), .K(and_58_out), .clk(button_10_out), .Q(j_k_ff_13_q[2]), .preset(and_63_out));  // open: Qn, reset
  Button button_11 (.out(button_11_out));
  and and_64 (and_64_out, button_9_out, j_k_ff_10_q[2]);
  J_K_Flip_Flop j_k_ff_20 (
    .J(and_59_out), .K(and_59_out), .clk(button_8_out), .Q(j_k_ff_20_q), .preset(and_64_out),
    .reset(or_13_out));  // open: Qn
  or or_13 (or_13_out, and_39_out, and_40_out, and_65_out);
  and and_65 (and_65_out, button_9_out, not_35_out);
  not not_35 (not_35_out, j_k_ff_10_q[2]);
  and and_66 (and_66_out, button_8_out, j_k_ff_20_q);
  J_K_Flip_Flop j_k_ff_21 (
    .J(and_60_out), .K(and_60_out), .clk(button_9_out), .Q(j_k_ff_10_q[2]), .preset(and_66_out),
    .reset(or_14_out));  // open: Qn
  or or_14 (or_14_out, and_39_out, and_40_out, and_67_out);
  and and_67 (and_67_out, button_8_out, not_36_out);
  not not_36 (not_36_out, j_k_ff_20_q);
  not not_37 (not_37_out, j_k_ff_10_q[2]);
  and and_68 (and_68_out, buffer_41_out, j_k_ff_12_q[2]);
  J_K_Flip_Flop j_k_ff_22 (
    .J(and_61_out), .K(and_61_out), .clk(and_39_out), .Q(j_k_ff_22_q), .preset(and_68_out), .reset(or_15_out));  // open: Qn
  or or_15 (or_15_out, and_45_out, and_46_out, and_69_out);
  and and_69 (and_69_out, buffer_41_out, not_38_out);
  not not_38 (not_38_out, j_k_ff_12_q[2]);
  and and_70 (and_70_out, buffer_40_out, j_k_ff_22_q);
  J_K_Flip_Flop j_k_ff_23 (
    .J(and_62_out), .K(and_62_out), .clk(and_40_out), .Q(j_k_ff_12_q[2]), .preset(and_70_out),
    .reset(or_16_out));  // open: Qn
  or or_16 (or_16_out, and_45_out, and_46_out, and_71_out);
  and and_71 (and_71_out, buffer_40_out, not_39_out);
  not not_39 (not_39_out, j_k_ff_22_q);
  not not_40 (not_40_out, j_k_ff_12_q[2]);
  J_K_Flip_Flop j_k_ff_24 (
    .J(in_12), .K(in_12), .clk(button_11_out), .Q(j_k_ff_24_q), .reset(and_89_out));  // open: Qn, preset
  not not_41 (not_41_out, j_k_ff_10_q[2]);
  not not_42 (not_42_out, j_k_ff_12_q[2]);
  Hex_Digit_Display hex_digit_display_2 (.value({in_9, j_k_ff_13_q}));  // open: dp
  J_K_Flip_Flop j_k_ff_25 (
    .J(j_k_ff_24_q), .K(j_k_ff_24_q), .clk(button_11_out), .Q(j_k_ff_25_q), .reset(and_89_out));  // open: Qn, preset
  and and_72 (and_72_out, and_40_out, in_22);
  and and_73 (and_73_out, and_59_out, j_k_ff_20_q);
  and and_74 (and_74_out, and_40_out, in_34);
  and and_75 (and_75_out, and_60_out, not_41_out);
  and and_76 (and_76_out, and_46_out, in_42);
  and and_77 (and_77_out, and_61_out, j_k_ff_22_q);
  and and_78 (and_78_out, and_46_out, in_53);
  and and_79 (and_79_out, and_62_out, not_42_out);
  and and_80 (and_80_out, j_k_ff_24_q, j_k_ff_25_q);
  and and_81 (and_81_out, button_9_out, j_k_ff_10_q[3]);
  or or_17 (or_17_out, and_72_out, and_81_out);
  J_K_Flip_Flop j_k_ff_26 (
    .J(and_73_out), .K(and_73_out), .clk(button_8_out), .Q(j_k_ff_26_q), .preset(or_17_out), .reset(or_18_out));  // open: Qn
  or or_18 (or_18_out, and_39_out, and_82_out);
  and and_82 (and_82_out, button_9_out, not_43_out);
  not not_43 (not_43_out, j_k_ff_10_q[3]);
  and and_83 (and_83_out, button_8_out, j_k_ff_26_q);
  or or_19 (or_19_out, and_74_out, and_83_out);
  J_K_Flip_Flop j_k_ff_27 (
    .J(and_75_out), .K(and_75_out), .clk(button_9_out), .Q(j_k_ff_10_q[3]), .preset(or_19_out),
    .reset(or_20_out));  // open: Qn
  or or_20 (or_20_out, and_39_out, and_84_out);
  and and_84 (and_84_out, button_8_out, not_44_out);
  not not_44 (not_44_out, j_k_ff_26_q);
  and and_85 (and_85_out, buffer_41_out, j_k_ff_12_q[3]);
  or or_21 (or_21_out, and_76_out, and_85_out);
  J_K_Flip_Flop j_k_ff_28 (
    .J(and_77_out), .K(and_77_out), .clk(and_39_out), .Q(j_k_ff_28_q), .preset(or_21_out), .reset(or_22_out));  // open: Qn
  or or_22 (or_22_out, and_45_out, and_86_out);
  and and_86 (and_86_out, buffer_41_out, not_45_out);
  not not_45 (not_45_out, j_k_ff_12_q[3]);
  and and_87 (and_87_out, buffer_40_out, j_k_ff_28_q);
  or or_23 (or_23_out, and_78_out, and_87_out);
  J_K_Flip_Flop j_k_ff_29 (
    .J(and_79_out), .K(and_79_out), .clk(and_40_out), .Q(j_k_ff_12_q[3]), .preset(or_23_out),
    .reset(or_24_out));  // open: Qn
  or or_24 (or_24_out, and_45_out, and_88_out);
  and and_88 (and_88_out, buffer_40_out, not_46_out);
  not not_46 (not_46_out, j_k_ff_28_q);
  J_K_Flip_Flop j_k_ff_30 (
    .J(and_80_out), .K(and_80_out), .clk(button_11_out), .Q(j_k_ff_30_q), .reset(and_89_out));  // open: Qn, preset
  and and_89 (and_89_out, j_k_ff_24_q, j_k_ff_25_q, j_k_ff_30_q);
  Hex_Digit_Display hex_digit_display_3 (.value(j_k_ff_10_q));  // open: dp
  Hex_Digit_Display hex_digit_display_4 (.value(j_k_ff_12_q));  // open: dp
  Button button_12 (.out(button_12_out));
  Button button_13 (.out(button_13_out));
  and and_90 (and_90_out, button_13_out, j_k_ff_32_q[0]);
  and and_91 (and_91_out, and_97_out, in_19);
  or or_25 (or_25_out, and_91_out, and_90_out);
  J_K_Flip_Flop j_k_ff_31 (
    .J(in_23), .K(in_23), .clk(button_12_out), .Q(j_k_ff_31_q), .preset(or_25_out), .reset(or_26_out));  // open: Qn
  or or_26 (or_26_out, and_96_out, and_97_out, and_92_out);
  and and_92 (and_92_out, button_13_out, not_47_out);
  not not_47 (not_47_out, j_k_ff_32_q[0]);
  and and_93 (and_93_out, button_12_out, j_k_ff_31_q);
  and and_94 (and_94_out, and_97_out, in_31);
  or or_27 (or_27_out, and_94_out, and_93_out);
  J_K_Flip_Flop j_k_ff_32 (
    .J(in_23), .K(in_23), .clk(button_13_out), .Q(j_k_ff_32_q[0]), .preset(or_27_out), .reset(or_28_out));  // open: Qn
  or or_28 (or_28_out, and_96_out, and_97_out, and_95_out);
  and and_95 (and_95_out, button_12_out, not_48_out);
  not not_48 (not_48_out, j_k_ff_31_q);
  and and_96 (and_96_out, not_51_out, j_k_ff_32_q[1], not_63_out, j_k_ff_32_q[3]);
  and and_97 (and_97_out, j_k_ff_32_q[0], j_k_ff_32_q[1], j_k_ff_32_q[2], j_k_ff_32_q[3]);
  and and_98 (and_98_out, nor_16_out, j_k_ff_34_q[0]);
  and and_99 (and_99_out, and_105_out, in_37);
  or or_29 (or_29_out, and_99_out, and_98_out);
  J_K_Flip_Flop j_k_ff_33 (
    .J(in_43), .K(in_43), .clk(and_96_out), .Q(j_k_ff_33_q), .preset(or_29_out), .reset(or_30_out));  // open: Qn
  or or_30 (or_30_out, and_104_out, and_105_out, and_100_out);
  and and_100 (and_100_out, nor_16_out, not_49_out);
  not not_49 (not_49_out, j_k_ff_34_q[0]);
  and and_101 (and_101_out, nor_15_out, j_k_ff_33_q);
  and and_102 (and_102_out, and_105_out, in_47);
  or or_31 (or_31_out, and_102_out, and_101_out);
  J_K_Flip_Flop j_k_ff_34 (
    .J(in_43), .K(in_43), .clk(and_97_out), .Q(j_k_ff_34_q[0]), .preset(or_31_out), .reset(or_32_out));  // open: Qn
  or or_32 (or_32_out, and_104_out, and_105_out, and_103_out);
  and and_103 (and_103_out, nor_15_out, not_50_out);
  not not_50 (not_50_out, j_k_ff_33_q);
  and and_104 (and_104_out, not_52_out, j_k_ff_34_q[1], not_66_out, j_k_ff_34_q[3]);
  and and_105 (and_105_out, j_k_ff_34_q[0], j_k_ff_34_q[1], j_k_ff_34_q[2], j_k_ff_34_q[3]);
  not not_51 (not_51_out, j_k_ff_32_q[0]);
  nor nor_15 (nor_15_out, and_97_out, nor_16_out);
  nor nor_16 (nor_16_out, nor_15_out, and_96_out);
  not not_52 (not_52_out, j_k_ff_34_q[0]);
  not not_53 (not_53_out, j_k_ff_32_q[0]);
  not not_54 (not_54_out, j_k_ff_34_q[0]);
  and and_106 (and_106_out, button_13_out, j_k_ff_32_q[1]);
  J_K_Flip_Flop j_k_ff_35 (
    .J(j_k_ff_31_q), .K(j_k_ff_31_q), .clk(button_12_out), .Q(j_k_ff_35_q), .preset(and_106_out),
    .reset(or_33_out));  // open: Qn
  or or_33 (or_33_out, and_96_out, and_107_out);
  and and_107 (and_107_out, button_13_out, not_55_out);
  not not_55 (not_55_out, j_k_ff_32_q[1]);
  and and_108 (and_108_out, button_12_out, j_k_ff_35_q);
  J_K_Flip_Flop j_k_ff_36 (
    .J(not_53_out), .K(not_53_out), .clk(button_13_out), .Q(j_k_ff_32_q[1]), .preset(and_108_out),
    .reset(or_34_out));  // open: Qn
  or or_34 (or_34_out, and_96_out, and_109_out);
  and and_109 (and_109_out, button_12_out, not_56_out);
  not not_56 (not_56_out, j_k_ff_35_q);
  and and_110 (and_110_out, nor_16_out, j_k_ff_34_q[1]);
  J_K_Flip_Flop j_k_ff_37 (
    .J(j_k_ff_33_q), .K(j_k_ff_33_q), .clk(and_96_out), .Q(j_k_ff_37_q), .preset(and_110_out),
    .reset(or_35_out));  // open: Qn
  or or_35 (or_35_out, and_104_out, and_111_out);
  and and_111 (and_111_out, nor_16_out, not_57_out);
  not not_57 (not_57_out, j_k_ff_34_q[1]);
  and and_112 (and_112_out, nor_15_out, j_k_ff_37_q);
  J_K_Flip_Flop j_k_ff_38 (
    .J(not_54_out), .K(not_54_out), .clk(and_97_out), .Q(j_k_ff_34_q[1]), .preset(and_112_out),
    .reset(or_36_out));  // open: Qn
  or or_36 (or_36_out, and_104_out, and_113_out);
  and and_113 (and_113_out, nor_15_out, not_58_out);
  not not_58 (not_58_out, j_k_ff_37_q);
  not not_59 (not_59_out, j_k_ff_32_q[1]);
  not not_60 (not_60_out, j_k_ff_34_q[1]);
  and and_114 (and_114_out, j_k_ff_31_q, j_k_ff_35_q);
  and and_115 (and_115_out, not_53_out, not_59_out);
  and and_116 (and_116_out, j_k_ff_33_q, j_k_ff_37_q);
  and and_117 (and_117_out, not_54_out, not_60_out);
  J_K_Flip_Flop j_k_ff_39 (
    .J(and_114_out), .K(and_114_out), .clk(button_12_out), .Q(j_k_ff_39_q), .preset(and_118_out),
    .reset(or_37_out));  // open: Qn
  J_K_Flip_Flop j_k_ff_40 (
    .J(and_115_out), .K(and_115_out), .clk(button_13_out), .Q(j_k_ff_32_q[2]), .preset(and_120_out),
    .reset(or_38_out));  // open: Qn
  J_K_Flip_Flop j_k_ff_41 (
    .J(and_116_out), .K(and_116_out), .clk(and_96_out), .Q(j_k_ff_41_q), .preset(and_122_out),
    .reset(or_39_out));  // open: Qn
  J_K_Flip_Flop j_k_ff_42 (
    .J(and_117_out), .K(and_117_out), .clk(and_97_out), .Q(j_k_ff_34_q[2]), .preset(and_124_out),
    .reset(or_40_out));  // open: Qn
  and and_118 (and_118_out, button_13_out, j_k_ff_32_q[2]);
  or or_37 (or_37_out, and_96_out, and_97_out, and_119_out);
  and and_119 (and_119_out, button_13_out, not_61_out);
  not not_61 (not_61_out, j_k_ff_32_q[2]);
  and and_120 (and_120_out, button_12_out, j_k_ff_39_q);
  or or_38 (or_38_out, and_96_out, and_97_out, and_121_out);
  and and_121 (and_121_out, button_12_out, not_62_out);
  not not_62 (not_62_out, j_k_ff_39_q);
  not not_63 (not_63_out, j_k_ff_32_q[2]);
  and and_122 (and_122_out, nor_16_out, j_k_ff_34_q[2]);
  or or_39 (or_39_out, and_104_out, and_105_out, and_123_out);
  and and_123 (and_123_out, nor_16_out, not_64_out);
  not not_64 (not_64_out, j_k_ff_34_q[2]);
  and and_124 (and_124_out, nor_15_out, j_k_ff_41_q);
  or or_40 (or_40_out, and_104_out, and_105_out, and_125_out);
  and and_125 (and_125_out, nor_15_out, not_65_out);
  not not_65 (not_65_out, j_k_ff_41_q);
  not not_66 (not_66_out, j_k_ff_34_q[2]);
  not not_67 (not_67_out, j_k_ff_32_q[2]);
  not not_68 (not_68_out, j_k_ff_34_q[2]);
  and and_126 (and_126_out, and_114_out, j_k_ff_39_q);
  and and_127 (and_127_out, and_115_out, not_67_out);
  and and_128 (and_128_out, and_116_out, j_k_ff_41_q);
  and and_129 (and_129_out, and_117_out, not_68_out);
  and and_130 (and_130_out, button_13_out, j_k_ff_32_q[3]);
  and and_131 (and_131_out, and_97_out, in_20);
  or or_41 (or_41_out, and_131_out, and_130_out);
  J_K_Flip_Flop j_k_ff_43 (
    .J(and_126_out), .K(and_126_out), .clk(button_12_out), .Q(j_k_ff_43_q), .preset(or_41_out),
    .reset(or_42_out));  // open: Qn
  or or_42 (or_42_out, and_96_out, and_132_out);
  and and_132 (and_132_out, button_13_out, not_69_out);
  and and_133 (and_133_out, button_12_out, j_k_ff_43_q);
  and and_134 (and_134_out, and_97_out, in_32);
  or or_43 (or_43_out, and_134_out, and_133_out);
  J_K_Flip_Flop j_k_ff_44 (
    .J(and_127_out), .K(and_127_out), .clk(button_13_out), .Q(j_k_ff_32_q[3]), .preset(or_43_out),
    .reset(or_44_out));  // open: Qn
  or or_44 (or_44_out, and_96_out, and_135_out);
  and and_135 (and_135_out, button_12_out, not_70_out);
  and and_136 (and_136_out, nor_16_out, j_k_ff_34_q[3]);
  and and_137 (and_137_out, and_105_out, in_38);
  or or_45 (or_45_out, and_137_out, and_136_out);
  J_K_Flip_Flop j_k_ff_45 (
    .J(and_128_out), .K(and_128_out), .clk(and_96_out), .Q(j_k_ff_45_q), .preset(or_45_out), .reset(or_46_out));  // open: Qn
  or or_46 (or_46_out, and_104_out, and_138_out);
  and and_138 (and_138_out, nor_16_out, not_71_out);
  and and_139 (and_139_out, nor_15_out, j_k_ff_45_q);
  and and_140 (and_140_out, and_105_out, in_48);
  or or_47 (or_47_out, and_140_out, and_139_out);
  J_K_Flip_Flop j_k_ff_46 (
    .J(and_129_out), .K(and_129_out), .clk(and_97_out), .Q(j_k_ff_34_q[3]), .preset(or_47_out),
    .reset(or_48_out));  // open: Qn
  or or_48 (or_48_out, and_104_out, and_141_out);
  and and_141 (and_141_out, nor_15_out, not_72_out);
  not not_69 (not_69_out, j_k_ff_32_q[3]);
  not not_70 (not_70_out, j_k_ff_43_q);
  not not_71 (not_71_out, j_k_ff_34_q[3]);
  not not_72 (not_72_out, j_k_ff_45_q);
  Hex_Digit_Display hex_digit_display_5 (.value(j_k_ff_32_q));  // open: dp
  Hex_Digit_Display hex_digit_display_6 (.value(j_k_ff_34_q));  // open: dp
  nor nor_17 (nor_17_out, and_142_out, nor_18_out);
  nor nor_18 (nor_18_out, nor_17_out, and_143_out);
  and and_142 (and_142_out, and_144_out, and_144_out);
  and and_143 (and_143_out, and_144_out, not_73_out);
  not not_73 (not_73_out, and_144_out);
  Button button_14 (.out(button_14_out));
  nor nor_19 (nor_19_out, in_36, nor_20_out);
  nor nor_20 (nor_20_out, nor_19_out, not_74_out);
  J_K_Flip_Flop j_k_ff_47 (.J(in_35), .K(in_35), .clk(button_14_out), .Q(j_k_ff_47_q));  // open: Qn, preset, reset
  not not_74 (not_74_out, in_36);
  J_K_Flip_Flop j_k_ff_48 (
    .J(in_17), .K(in_17), .clk(button_15_out), .Q(j_k_ff_48_q[0]), .preset(and_148_out), .reset(and_145_out));  // open: Qn
  Button button_15 (.out(button_15_out));
  and and_144 (and_144_out, j_k_ff_48_q[0], j_k_ff_48_q[1], j_k_ff_48_q[2], j_k_ff_48_q[3]);
  not not_75 (not_75_out, j_k_ff_48_q[0]);
  and and_145 (and_145_out, not_75_out, j_k_ff_48_q[1], not_76_out, j_k_ff_48_q[3]);
  not not_76 (not_76_out, j_k_ff_48_q[2]);
  J_K_Flip_Flop j_k_ff_49 (
    .J(in_29), .K(in_29), .clk(and_144_out), .Q(j_k_ff_49_q[0]), .preset(and_149_out), .reset(and_147_out));  // open: Qn
  and and_146 (and_146_out, j_k_ff_49_q[0], j_k_ff_49_q[1], j_k_ff_49_q[2], j_k_ff_49_q[3]);
  not not_77 (not_77_out, j_k_ff_49_q[0]);
  and and_147 (and_147_out, not_77_out, j_k_ff_49_q[1], not_78_out, j_k_ff_49_q[3]);
  not not_78 (not_78_out, j_k_ff_49_q[2]);
  not not_79 (not_79_out, j_k_ff_47_q);
  and and_148 (and_148_out, and_144_out, in_13);
  and and_149 (and_149_out, and_146_out, in_25);
  not not_80 (not_80_out, j_k_ff_49_q[0]);
  nor nor_21 (nor_21_out, not_79_out, nor_22_out);
  nor nor_22 (nor_22_out, nor_21_out, j_k_ff_47_q);
  J_K_Flip_Flop j_k_ff_50 (
    .J(not_81_out), .K(not_81_out), .clk(button_15_out), .Q(j_k_ff_48_q[1]), .reset(or_49_out));  // open: Qn, preset
  not not_81 (not_81_out, j_k_ff_48_q[0]);
  J_K_Flip_Flop j_k_ff_51 (
    .J(not_80_out), .K(not_80_out), .clk(and_144_out), .Q(j_k_ff_49_q[1]), .reset(or_50_out));  // open: Qn, preset
  D_Flip_Flop d_ff_7 (.D(nor_21_out), .clk(button_14_out), .Q(d_ff_7_q));  // open: Qn, preset, reset
  nor nor_23 (nor_23_out, and_152_out, nor_24_out);
  nor nor_24 (nor_24_out, nor_23_out, and_153_out);
  nor nor_25 (nor_25_out, and_154_out, nor_26_out);
  nor nor_26 (nor_26_out, nor_25_out, and_155_out);
  or or_49 (or_49_out, and_144_out, and_145_out);
  not not_82 (not_82_out, j_k_ff_49_q[1]);
  or or_50 (or_50_out, and_146_out, and_147_out);
  J_K_Flip_Flop j_k_ff_52 (.J(in_11), .K(in_11), .clk(undriven_6), .Q(j_k_ff_52_q));  // open: Qn, preset, reset
  and and_150 (and_150_out, not_81_out, not_83_out);
  not not_83 (not_83_out, j_k_ff_48_q[1]);
  and and_151 (and_151_out, not_80_out, not_82_out);
  and and_152 (and_152_out, undriven_5, undriven_5);
  and and_153 (and_153_out, undriven_5, not_86_out);
  and and_154 (and_154_out, undriven_4, undriven_4);
  and and_155 (and_155_out, undriven_4, not_87_out);
  J_K_Flip_Flop j_k_ff_53 (
    .J(and_150_out), .K(and_150_out), .clk(button_15_out), .Q(j_k_ff_48_q[2]), .reset(or_51_out));  // open: Qn, preset
  or or_51 (or_51_out, and_144_out, and_145_out);
  J_K_Flip_Flop j_k_ff_54 (
    .J(and_151_out), .K(and_151_out), .clk(and_144_out), .Q(j_k_ff_49_q[2]), .reset(or_52_out));  // open: Qn, preset
  or or_52 (or_52_out, and_146_out, and_147_out);
  J_K_Flip_Flop j_k_ff_55 (
    .J(j_k_ff_52_q), .K(j_k_ff_52_q), .clk(undriven_6), .Q(j_k_ff_55_q));  // open: Qn, preset, reset
  not not_84 (not_84_out, j_k_ff_48_q[2]);
  not not_85 (not_85_out, j_k_ff_49_q[2]);
  not not_86 (not_86_out, undriven_5);
  not not_87 (not_87_out, undriven_4);
  and and_156 (and_156_out, and_144_out, in_15);
  and and_157 (and_157_out, and_150_out, not_84_out);
  J_K_Flip_Flop j_k_ff_56 (
    .J(and_157_out), .K(and_157_out), .clk(button_15_out), .Q(j_k_ff_48_q[3]), .preset(and_156_out),
    .reset(and_145_out));  // open: Qn
  and and_158 (and_158_out, and_146_out, in_27);
  and and_159 (and_159_out, and_151_out, not_85_out);
  J_K_Flip_Flop j_k_ff_57 (
    .J(and_159_out), .K(and_159_out), .clk(and_144_out), .Q(j_k_ff_49_q[3]), .preset(and_158_out),
    .reset(and_147_out));  // open: Qn
  and and_160 (and_160_out, j_k_ff_52_q, j_k_ff_55_q);
  J_K_Flip_Flop j_k_ff_58 (
    .J(and_160_out), .K(and_160_out), .clk(undriven_6), .Q(j_k_ff_58_q));  // open: Qn, preset, reset
  Button button_16 (.out(button_16_out));
  and and_161 (and_161_out, and_168_out, in_39);
  J_K_Flip_Flop j_k_ff_59 (
    .J(in_44), .K(in_44), .clk(button_16_out), .Q(j_k_ff_59_q), .preset(or_53_out), .reset(or_54_out));  // open: Qn
  and and_162 (and_162_out, and_168_out, in_50);
  J_K_Flip_Flop j_k_ff_60 (
    .J(in_44), .K(in_44), .clk(button_16_out), .Q(j_k_ff_60_q[0]), .preset(or_55_out), .reset(or_56_out));  // open: Qn
  Hex_Digit_Display hex_digit_display_7 (.value(j_k_ff_48_q));  // open: dp
  Hex_Digit_Display hex_digit_display_8 (.value(j_k_ff_49_q));  // open: dp
  and and_163 (and_163_out, button_16_out, j_k_ff_60_q[0]);
  or or_53 (or_53_out, and_161_out, and_163_out);
  or or_54 (or_54_out, and_167_out, and_164_out);
  and and_164 (and_164_out, button_16_out, not_88_out);
  not not_88 (not_88_out, j_k_ff_60_q[0]);
  and and_165 (and_165_out, button_16_out, j_k_ff_59_q);
  or or_55 (or_55_out, and_162_out, and_165_out);
  or or_56 (or_56_out, and_167_out, and_166_out);
  and and_166 (and_166_out, button_16_out, not_89_out);
  not not_89 (not_89_out, j_k_ff_59_q);
  and and_167 (and_167_out, not_91_out, j_k_ff_60_q[1], not_101_out, j_k_ff_60_q[3]);
  and and_168 (and_168_out, j_k_ff_60_q[0], j_k_ff_60_q[1], j_k_ff_60_q[2], j_k_ff_60_q[3]);
  not not_90 (not_90_out, j_k_ff_60_q[0]);
  not not_91 (not_91_out, j_k_ff_60_q[0]);
  and and_169 (and_169_out, j_k_ff_61_q[0], j_k_ff_61_q[1], j_k_ff_61_q[2], j_k_ff_61_q[3]);
  and and_170 (and_170_out, not_92_out, j_k_ff_61_q[1], not_93_out, j_k_ff_61_q[3]);
  and and_171 (and_171_out, j_k_ff_62_q[0], j_k_ff_62_q[1], j_k_ff_62_q[2], j_k_ff_62_q[3]);
  and and_172 (and_172_out, not_94_out, j_k_ff_62_q[1], not_95_out, j_k_ff_62_q[3]);
  and and_173 (and_173_out, and_169_out, in_14);
  J_K_Flip_Flop j_k_ff_61 (
    .J(in_18), .K(in_18), .clk(button_17_out), .Q(j_k_ff_61_q[0]), .preset(and_173_out), .reset(and_170_out));  // open: Qn
  Button button_17 (.out(button_17_out));
  not not_92 (not_92_out, j_k_ff_61_q[0]);
  not not_93 (not_93_out, j_k_ff_61_q[2]);
  and and_174 (and_174_out, and_171_out, in_26);
  J_K_Flip_Flop j_k_ff_62 (
    .J(in_30), .K(in_30), .clk(and_170_out), .Q(j_k_ff_62_q[0]), .preset(and_174_out), .reset(and_172_out));  // open: Qn
  not not_94 (not_94_out, j_k_ff_62_q[0]);
  not not_95 (not_95_out, j_k_ff_62_q[2]);
  and and_175 (and_175_out, button_16_out, j_k_ff_60_q[1]);
  J_K_Flip_Flop j_k_ff_63 (
    .J(j_k_ff_59_q), .K(j_k_ff_59_q), .clk(button_16_out), .Q(j_k_ff_63_q), .preset(and_175_out),
    .reset(or_57_out));  // open: Qn
  or or_57 (or_57_out, and_167_out, and_168_out, and_176_out);
  and and_176 (and_176_out, button_16_out, not_96_out);
  and and_177 (and_177_out, button_16_out, j_k_ff_63_q);
  J_K_Flip_Flop j_k_ff_64 (
    .J(not_90_out), .K(not_90_out), .clk(button_16_out), .Q(j_k_ff_60_q[1]), .preset(and_177_out),
    .reset(or_58_out));  // open: Qn
  or or_58 (or_58_out, and_167_out, and_168_out, and_178_out);
  and and_178 (and_178_out, button_16_out, not_97_out);
  not not_96 (not_96_out, j_k_ff_60_q[1]);
  not not_97 (not_97_out, j_k_ff_63_q);
  J_K_Flip_Flop j_k_ff_65 (
    .J(j_k_ff_61_q[0]), .K(j_k_ff_61_q[0]), .clk(button_17_out), .Q(j_k_ff_61_q[1]), .reset(or_59_out));  // open: Qn, preset
  or or_59 (or_59_out, and_169_out, and_170_out);
  J_K_Flip_Flop j_k_ff_66 (
    .J(j_k_ff_62_q[0]), .K(j_k_ff_62_q[0]), .clk(and_170_out), .Q(j_k_ff_62_q[1]), .reset(or_60_out));  // open: Qn, preset
  or or_60 (or_60_out, and_171_out, and_172_out);
  not not_98 (not_98_out, j_k_ff_60_q[1]);
  and and_179 (and_179_out, j_k_ff_59_q, j_k_ff_63_q);
  and and_180 (and_180_out, not_90_out, not_98_out);
  and and_181 (and_181_out, j_k_ff_61_q[0], j_k_ff_61_q[1]);
  J_K_Flip_Flop j_k_ff_67 (
    .J(and_181_out), .K(and_181_out), .clk(button_17_out), .Q(j_k_ff_61_q[2]), .reset(or_64_out));  // open: Qn, preset
  and and_182 (and_182_out, j_k_ff_62_q[0], j_k_ff_62_q[1]);
  J_K_Flip_Flop j_k_ff_68 (
    .J(and_182_out), .K(and_182_out), .clk(and_170_out), .Q(j_k_ff_62_q[2]), .reset(or_61_out));  // open: Qn, preset
  or or_61 (or_61_out, and_171_out, and_172_out);
  and and_183 (and_183_out, button_16_out, j_k_ff_60_q[2]);
  J_K_Flip_Flop j_k_ff_69 (
    .J(and_179_out), .K(and_179_out), .clk(button_16_out), .Q(j_k_ff_69_q), .preset(and_183_out),
    .reset(or_62_out));  // open: Qn
  or or_62 (or_62_out, and_167_out, and_168_out, and_184_out);
  and and_184 (and_184_out, button_16_out, not_99_out);
  not not_99 (not_99_out, j_k_ff_60_q[2]);
  and and_185 (and_185_out, button_16_out, j_k_ff_69_q);
  J_K_Flip_Flop j_k_ff_70 (
    .J(and_180_out), .K(and_180_out), .clk(button_16_out), .Q(j_k_ff_60_q[2]), .preset(and_185_out),
    .reset(or_63_out));  // open: Qn
  or or_63 (or_63_out, and_167_out, and_168_out, and_186_out);
  and and_186 (and_186_out, button_16_out, not_100_out);
  not not_100 (not_100_out, j_k_ff_69_q);
  not not_101 (not_101_out, j_k_ff_60_q[2]);
  or or_64 (or_64_out, and_169_out, and_170_out);
  and and_187 (and_187_out, and_181_out, j_k_ff_61_q[2]);
  and and_188 (and_188_out, and_182_out, j_k_ff_62_q[2]);
  J_K_Flip_Flop j_k_ff_71 (
    .J(and_188_out), .K(and_188_out), .clk(and_170_out), .Q(j_k_ff_62_q[3]), .preset(and_190_out),
    .reset(and_172_out));  // open: Qn
  not not_102 (not_102_out, j_k_ff_60_q[2]);
  and and_189 (and_189_out, and_169_out, in_16);
  J_K_Flip_Flop j_k_ff_72 (
    .J(and_187_out), .K(and_187_out), .clk(button_17_out), .Q(j_k_ff_61_q[3]), .preset(and_189_out),
    .reset(and_170_out));  // open: Qn
  and and_190 (and_190_out, and_171_out, in_28);
  and and_191 (and_191_out, and_168_out, in_40);
  and and_192 (and_192_out, and_179_out, j_k_ff_69_q);
  and and_193 (and_193_out, and_168_out, in_51);
  and and_194 (and_194_out, and_180_out, not_102_out);
  and and_195 (and_195_out, button_16_out, j_k_ff_60_q[3]);
  or or_65 (or_65_out, and_191_out, and_195_out);
  J_K_Flip_Flop j_k_ff_73 (
    .J(and_192_out), .K(and_192_out), .clk(button_16_out), .Q(j_k_ff_73_q), .preset(or_65_out),
    .reset(or_66_out));  // open: Qn
  or or_66 (or_66_out, and_167_out, and_196_out);
  and and_196 (and_196_out, button_16_out, not_103_out);
  not not_103 (not_103_out, j_k_ff_60_q[3]);
  and and_197 (and_197_out, button_16_out, j_k_ff_73_q);
  or or_67 (or_67_out, and_193_out, and_197_out);
  J_K_Flip_Flop j_k_ff_74 (
    .J(and_194_out), .K(and_194_out), .clk(button_16_out), .Q(j_k_ff_60_q[3]), .preset(or_67_out),
    .reset(or_68_out));  // open: Qn
  or or_68 (or_68_out, and_167_out, and_198_out);
  and and_198 (and_198_out, button_16_out, not_104_out);
  not not_104 (not_104_out, j_k_ff_73_q);
  Hex_Digit_Display hex_digit_display_9 (.value(j_k_ff_61_q));  // open: dp
  Hex_Digit_Display hex_digit_display_10 (.value(j_k_ff_62_q));  // open: dp
  Hex_Digit_Display hex_digit_display_11 (.value(j_k_ff_60_q));  // open: dp

  // Notes on the sheet:
  //   IS PLAYING
  //   IS PAUSED
  //   IS PLAYING
  //   IS PAUSED
  //   up
  //   down
  //   sync down
  //   sync up
endmodule
