// Logisim project encoders.circ as structural Verilog: 1 circuit, main circuit main
module main (
  input  _1,
  input  _2,
  input  _3,
  input  _4,
  input  _5,
  input  _6,
  input  _7,
  input  _8,
  input  _8_2,
  input  _7_2,
  input  _6_2,
  input  _5_2,
  input  _4_2,
  input  _3_2,
  input  _2_2,
  input  _1_2,
  input  _8_3,
  input  _7_3,
  input  _6_3,
  input  _5_3,
  input  _4_3,
  input  _3_3,
  input  _2_3,
  input  _1_3
);

  wire and_1_out, and_3_out, and_4_out, and_5_out, and_6_out, nor_1_out, not_1_out, not_2_out, not_3_out,
       not_4_out, or_1_out, or_2_out, or_3_out, or_4_out, or_5_out, or_6_out, or_7_out, or_8_out, or_9_out,
       or_10_out, or_11_out, undriven;

  not not_1 (not_1_out, _3);
  and and_1 (and_1_out, _2, not_1_out);
  // AND_Gate and_2 is placed but not wired
  not not_2 (not_2_out, _3_2);
  not not_3 (not_3_out, _5_2);
  not not_4 (not_4_out, _7_2);
  or or_1 (or_1_out, _2_3, _4_3, _6_3, _8_3);
  or or_2 (or_2_out, _3_3, _4_3, _7_3, _8_3);
  or or_3 (or_3_out, _5_3, _6_3, _7_3, _8_3);
  and and_3 (and_3_out, _2_2, not_2_out, not_3_out, not_4_out);
  and and_4 (and_4_out, _4_2, not_3_out, not_4_out);
  and and_5 (and_5_out, _6_2, not_4_out);
  or or_4 (or_4_out, _3_2, _4_2);
  nor nor_1 (nor_1_out, _5_2, _6_2);
  or or_5 (or_5_out, _7_2, _8_2);
  and and_6 (and_6_out, or_4_out, nor_1_out);
  or or_6 (or_6_out, and_3_out, and_4_out, and_5_out, _8_2);
  or or_7 (or_7_out, and_6_out, or_5_out);
  or or_8 (or_8_out, _5_2, _6_2, _7_2, _8_2);
  or or_9 (or_9_out, and_1_out, undriven, _8);
  or or_10 (or_10_out, _3, undriven, _8);
  buf or_11 (or_11_out, _8);  // OR_Gate

  // Notes on the sheet:
  //   1
  //   2
endmodule
